// Logisim project BASIC.circ as structural Verilog: 1 circuit, main circuit main
module main (
  input  in_1,
  input  in_2,
  input  in_3,
  input  in_4,
  output out_5,
  output out_6
);

  wire and_1_out, or_1_out;

  and and_1 (and_1_out, in_1, in_2);
  or or_1 (or_1_out, in_3, in_4);
  not not_1 (out_5, and_1_out);
  not not_2 (out_6, or_1_out);

  // Notes on the sheet:
  //   NAND GATE
  //   NOR GATE
  //   UNIVERSAL LOGIC GATES
  //   ASHUTOSH KUMAR
endmodule
