// Logisim project EXP_10(a)_ASHUTOSH_KR_SINGH.circ as structural Verilog: 1 circuit, main circuit main
module main (
  input  [2:0] in_1,
  input  Sub,
  input  Cin,
  input  A,
  input  B,
  input  Less,
  output Result,
  output Cout,
  output Set
);

  wire and_1_out, nor_1_out, or_1_out, xor_1_out, xor_2_out;

  xor xor_1 (xor_1_out, B, Sub);
  and and_1 (and_1_out, A, B);
  or or_1 (or_1_out, A, B);
  xor xor_2 (xor_2_out, A, B);
  nor nor_1 (nor_1_out, A, B);
  Adder #(.width(1)) adder_1 (.a(A), .b(xor_1_out), .out(Set), .cin(Cin), .cout(Cout));
  Multiplexer #(.select(3), .enable("false")) multiplexer_1 (
    .in0(and_1_out), .in1(or_1_out), .in2(xor_2_out), .in3(nor_1_out), .in4(Set), .in5(Less), .out(Result),
    .sel(in_1));  // open: in6, in7

  // Notes on the sheet:
  //   Exp 10: 4-bit ALU
  //   Ashutosh Kumar
  //   ALU Operations:
  //   AND
  //   OR
  //   XOR
  //   NOR
  //   ADD/SUB
endmodule
