// Logisim project EXP_10(b)_ASHUTOSH_KR_SINGH.circ as structural Verilog: 2 circuits, main circuit main
module main (
  input  [2:0] in_1,
  input  Sub,
  input  Cin,
  input  A,
  input  B,
  input  Less,
  output Result,
  output Cout,
  output Set
);

  wire and_1_out, nor_1_out, or_1_out, xor_1_out, xor_2_out;

  xor xor_1 (xor_1_out, B, Sub);
  and and_1 (and_1_out, A, B);
  or or_1 (or_1_out, A, B);
  xor xor_2 (xor_2_out, A, B);
  nor nor_1 (nor_1_out, A, B);
  Adder #(.width(1)) adder_1 (.a(A), .b(xor_1_out), .out(Set), .cin(Cin), .cout(Cout));
  Multiplexer #(.select(3), .enable("false")) multiplexer_1 (
    .in0(and_1_out), .in1(or_1_out), .in2(xor_2_out), .in3(nor_1_out), .in4(Set), .in5(Less), .out(Result),
    .sel(in_1));  // open: in6, in7

  // Notes on the sheet:
  //   4-bit ALU
  //   Ashutosh Kumar
  //   ALU Operations:
  //   AND
  //   OR
  //   XOR
  //   NOR
  //   ADD/SUB
endmodule

module _4_bit_ALU (
  input  Sub,
  input  [2:0] in_2,
  input  [3:0] A,
  input  [3:0] B,
  output [3:0] Result,
  output ZERO_FLAG
);

  wire main_1_cout, main_2_cout, main_3_cout, main_4_set;

  main main_1 (
    .A(A[0]), .B(B[0]), .Less(main_4_set), .Result(Result[0]), .Sub(Sub), .Cin(Sub), .in_1(in_2),
    .Cout(main_1_cout));  // open: Set
  main main_2 (
    .A(A[1]), .B(B[1]), .Less(1'b0), .Result(Result[1]), .Sub(Sub), .Cin(main_1_cout), .in_1(in_2),
    .Cout(main_2_cout));  // open: Set
  main main_3 (
    .A(A[2]), .B(B[2]), .Less(1'b0), .Result(Result[2]), .Sub(Sub), .Cin(main_2_cout), .in_1(in_2),
    .Cout(main_3_cout));  // open: Set
  main main_4 (
    .A(A[3]), .B(B[3]), .Less(1'b0), .Result(Result[3]), .Sub(Sub), .Cin(main_3_cout), .in_1(in_2),
    .Set(main_4_set));  // open: Cout
  nor nor_1 (ZERO_FLAG, Result[0], Result[1], Result[2], Result[3]);

  // Notes on the sheet:
  //   Function Selector
  //   4-bit ALU
  //   ALU Operations :
  //   000)AND
  //   001)OR
  //   010)XOR
  //   100)ADD/SUB
  //   Ashutosh Kumar
  //   Set Sub and Cin to high or 1 for SUB Operation
endmodule
