// Logisim project EXP_LOGICGATE.circ as structural Verilog: 1 circuit, main circuit main
module main (
  input  in_1,
  input  in_2,
  input  in_3,
  input  in_4,
  input  in_5,
  input  in_6,
  input  in_7,
  input  in_8,
  output out_9,
  output out_10
);

  wire and_1_out, and_2_out, and_3_out, and_4_out, not_1_out, not_2_out, not_3_out, not_4_out;

  not not_1 (not_1_out, in_2);
  not not_2 (not_2_out, in_3);
  not not_3 (not_3_out, in_7);
  not not_4 (not_4_out, in_8);
  and and_1 (and_1_out, in_1, not_1_out);
  and and_2 (and_2_out, not_2_out, in_4);
  and and_3 (and_3_out, in_5, in_6);
  and and_4 (and_4_out, not_3_out, not_4_out);
  or or_1 (out_9, and_1_out, and_2_out);
  or or_2 (out_10, and_3_out, and_4_out);

  // Notes on the sheet:
  //   EXCLUSIVE LOGIC GATES
  //   EX-OR LOGIC GATE
  //   EX-NOR LOGIC GATE
  //   ASHUTOSH KUMAR
endmodule
