// Logisim project exp2(b)coa_lab.circ as structural Verilog: 1 circuit, main circuit main
module main (
  input  in_1,
  input  in_2,
  input  in_3,
  input  in_4,
  input  in_5,
  input  in_6,
  input  in_7,
  input  in_8,
  input  in_9,
  input  in_10,
  input  in_11,
  output out_12,
  output out_13,
  output out_14,
  output out_15,
  output out_16,
  output out_17
);

  wire nor_2_out, nor_3_out, nor_4_out, nor_5_out, nor_6_out, nor_7_out, nor_9_out, nor_10_out, nor_13_out,
       nor_14_out, nor_15_out, nor_16_out, nor_17_out;

  nor nor_1 (out_12, in_3, in_3);
  nor nor_2 (nor_2_out, in_6, in_6);
  nor nor_3 (nor_3_out, in_8, in_8);
  nor nor_4 (nor_4_out, nor_2_out, nor_3_out);
  nor nor_5 (nor_5_out, in_10, in_11);
  nor nor_6 (nor_6_out, in_1, in_1);
  nor nor_7 (nor_7_out, in_5, in_5);
  nor nor_8 (out_15, nor_4_out, nor_4_out);
  nor nor_9 (nor_9_out, in_10, nor_5_out);
  nor nor_10 (nor_10_out, nor_5_out, in_11);
  nor nor_11 (out_17, nor_9_out, nor_10_out);
  nor nor_12 (out_13, nor_6_out, nor_7_out);
  nor nor_13 (nor_13_out, in_7, in_9);
  nor nor_14 (nor_14_out, in_7, nor_13_out);
  nor nor_15 (nor_15_out, nor_13_out, in_9);
  nor nor_16 (nor_16_out, in_2, in_4);
  nor nor_17 (nor_17_out, nor_14_out, nor_15_out);
  nor nor_18 (out_14, nor_16_out, nor_16_out);
  nor nor_19 (out_16, nor_17_out, nor_17_out);

  // Notes on the sheet:
  //   NOT Gate
  //   NAND Gate
  //   XNOR Gate
  //   AND Gate
  //   Different logic gates using NOR Gate
  //   XOR Gate
  //   Ashutosh Kumar
  //   OR Gate
endmodule
