// Logisim project exp3_ashutosh_kr_singh.circ as structural Verilog: 1 circuit, main circuit main
module main (
  input  in_1,
  input  in_2,
  input  in_3,
  input  in_4,
  output SUM,
  output CARRY,
  output SUM_2,
  output CARRY_2
);

  wire and_1_out, and_2_out, not_1_out, not_2_out;

  not not_1 (not_1_out, in_3);
  not not_2 (not_2_out, in_4);
  and and_1 (and_1_out, not_1_out, in_4);
  and and_2 (and_2_out, in_3, not_2_out);
  xor xor_1 (SUM, in_1, in_2);
  and and_3 (CARRY, in_1, in_2);
  or or_1 (SUM_2, and_1_out, and_2_out);
  and and_4 (CARRY_2, in_3, in_4);

  // Notes on the sheet:
  //   HALF ADDER
  //   HALF ADDER USING BASIC LOGIC GATES
  //   ASHUTOSH KUMAR 
endmodule
