// Logisim project exp3b_ashutosh_kr_singh.circ as structural Verilog: 1 circuit, main circuit main
module main (
  input  in_1,
  input  in_2,
  input  in_3,
  input  in_4,
  output SUM,
  output SUM_2,
  output CARRY,
  output CARRY_2
);

  wire nand_1_out, nand_2_out, nand_4_out, nand_5_out, nor_1_out, nor_2_out, nor_3_out, nor_4_out, nor_5_out,
       nor_6_out;

  nand nand_1 (nand_1_out, in_2, in_3);
  nand nand_2 (nand_2_out, in_2, in_3);
  nand nand_3 (CARRY, nand_2_out, nand_2_out);
  nand nand_4 (nand_4_out, in_2, nand_1_out);
  nand nand_5 (nand_5_out, nand_1_out, in_3);
  nand nand_6 (SUM, nand_4_out, nand_5_out);
  nor nor_1 (nor_1_out, in_1, in_4);
  nor nor_2 (nor_2_out, in_1, nor_1_out);
  nor nor_3 (nor_3_out, nor_1_out, in_4);
  nor nor_4 (nor_4_out, in_1, in_1);
  nor nor_5 (nor_5_out, in_4, in_4);
  nor nor_6 (nor_6_out, nor_2_out, nor_3_out);
  nor nor_7 (SUM_2, nor_6_out, nor_6_out);
  nor nor_8 (CARRY_2, nor_4_out, nor_5_out);

  // Notes on the sheet:
  //   (i)Using NAND Gate
  //   XOR Gate using NAND Gate
  //   AND Gate using NAND Gate
  //   HALF ADDER USING UNIVERSAL LOGIC GATES
  //   (ii)Using NOR Gate
  //   XOR Gate using NOR Gate
  //   AND Gate using NOR Gate
  //   ASHUTOSH KUMAR 
endmodule
