// Logisim project exp7b_ashutoshkrsingh.circ as structural Verilog: 1 circuit, main circuit main
module main (
  input  in_1,
  input  in_2,
  input  in_3,
  input  in_4,
  output out_5,
  output out_6,
  output out_7,
  output out_8,
  output out_9,
  output out_10,
  output out_11,
  output out_12
);

  wire not_1_out, not_2_out, not_3_out;

  not not_1 (not_1_out, in_1);
  not not_2 (not_2_out, in_2);
  not not_3 (not_3_out, in_3);
  and and_1 (out_5, not_1_out, not_2_out, not_3_out, in_4);
  and and_2 (out_6, not_1_out, not_2_out, in_3, in_4);
  and and_3 (out_7, not_1_out, in_2, not_3_out, in_4);
  and and_4 (out_8, not_1_out, in_2, in_3, in_4);
  and and_5 (out_9, in_1, not_2_out, not_3_out, in_4);
  and and_6 (out_10, in_1, not_2_out, in_3, in_4);
  and and_7 (out_11, in_1, in_2, not_3_out, in_4);
  and and_8 (out_12, in_1, in_2, in_3, in_4);

  // Notes on the sheet:
  //   3 to 8 Decoder
  //   Ashutosh Kumar
endmodule
