// Logisim project exp8(a)_ashutoshkrsingh.circ as structural Verilog: 1 circuit, main circuit main
module main (
  input  in_1,
  input  in_2,
  input  in_3,
  input  in_4,
  input  in_5,
  input  in_6,
  input  in_7,
  input  in_8,
  input  in_9,
  input  in_10,
  output out_11,
  output out_12,
  output out_13,
  output out_14,
  output out_15,
  output out_16,
  output out_17,
  output out_18,
  output out_19,
  output out_20
);

  wire and_1_out, and_2_out, and_3_out, and_4_out, and_5_out, and_6_out, and_7_out, and_8_out, and_9_out,
       and_10_out, clock_1_out, clock_2_out, clock_3_out, clock_4_out, clock_5_out;

  Clock clock_1 (.out(clock_1_out));
  Clock clock_2 (.out(clock_2_out));
  and and_1 (and_1_out, in_2, clock_1_out);
  and and_2 (and_2_out, clock_1_out, in_4);
  and and_3 (and_3_out, in_6, clock_2_out);
  and and_4 (and_4_out, clock_2_out, in_8);
  nor nor_1 (out_14, out_12, and_2_out);
  nor nor_2 (out_18, out_16, and_4_out);
  nor nor_3 (out_12, and_1_out, out_14);
  nor nor_4 (out_16, and_3_out, out_18);
  Clock clock_3 (.out(clock_3_out));
  and and_5 (and_5_out, in_9, clock_3_out);
  and and_6 (and_6_out, clock_3_out, in_10);
  Clock clock_4 (.out(clock_4_out));
  Clock clock_5 (.out(clock_5_out));
  nor nor_5 (out_19, and_5_out, out_20);
  nor nor_6 (out_20, out_19, and_6_out);
  and and_7 (and_7_out, in_1, clock_4_out);
  and and_8 (and_8_out, clock_4_out, in_3);
  and and_9 (and_9_out, in_5, clock_5_out);
  and and_10 (and_10_out, clock_5_out, in_7);
  nor nor_7 (out_13, out_11, and_8_out);
  nor nor_8 (out_15, and_9_out, out_17);
  nor nor_9 (out_17, out_15, and_10_out);
  nor nor_10 (out_11, and_7_out, out_13);

  // Notes on the sheet:
  //   (I)
  //   (II)
  //   Reset
  //   Set
  //   (V)
  //   SR Flip-Flop
  //   ASHUTOSH KUMAR
  //   (III)
  //   (IV)
  //   Hold
  //   Invalid
endmodule
