// Logisim project exp8(b)_ashutoshkrsingh.circ as structural Verilog: 1 circuit, main circuit main
module main (
  input  in_1,
  input  in_2,
  input  in_3,
  input  in_4,
  output out_5,
  output out_6,
  output out_7,
  output out_8
);

  wire clock_1_out, clock_2_out, nand_1_out, nand_2_out;

  Clock clock_1 (.out(clock_1_out));
  Clock clock_2 (.out(clock_2_out));
  nand nand_1 (nand_1_out, in_1, clock_1_out);
  nand nand_2 (nand_2_out, clock_1_out, in_2);
  S_R_Flip_Flop s_r_ff_1 (.S(in_3), .clk(clock_2_out), .R(in_4), .Q(out_7), .Qn(out_8));  // open: preset, reset, en
  nand nand_3 (out_5, nand_1_out, out_6);
  nand nand_4 (out_6, out_5, nand_2_out);

  // Notes on the sheet:
  //   Using NAND Gate only
  //   SR Flip-Flop
  //   Using built-in SR flip-flop
  //   ASHUTOSH KUMAR
endmodule
