// Logisim project exp_4A_ashutosh_kr_singh.circ as structural Verilog: 1 circuit, main circuit main
module main (
  input  in_1,
  input  in_2,
  input  in_3,
  output SUM,
  output Carry_Output
);

  wire and_1_out, and_2_out, xor_1_out;

  xor xor_1 (xor_1_out, in_1, in_2);
  and and_1 (and_1_out, xor_1_out, in_3);
  and and_2 (and_2_out, in_1, in_2);
  xor xor_2 (SUM, xor_1_out, in_3);
  or or_1 (Carry_Output, and_1_out, and_2_out);

  // Notes on the sheet:
  //   FULL ADDER
  //   USING TWO HALF ADDERS
  //   ASHUTOSH KUMAR
endmodule
