// Logisim project exp_4b_ashutosh_kr_singh.circ as structural Verilog: 1 circuit, main circuit main
module main (
  input  in_1,
  input  in_2,
  input  in_3,
  output SUM,
  output Carry_Output
);

  wire and_1_out, and_2_out, nand_1_out, nand_2_out, nand_3_out, nand_4_out, nand_5_out, nand_6_out,
       nand_7_out;

  nand nand_1 (nand_1_out, in_1, in_2);
  nand nand_2 (nand_2_out, in_1, nand_1_out);
  nand nand_3 (nand_3_out, nand_1_out, in_2);
  nand nand_4 (nand_4_out, nand_2_out, nand_3_out);
  and and_1 (and_1_out, in_1, in_2);
  and and_2 (and_2_out, nand_4_out, in_3);
  nand nand_5 (nand_5_out, nand_4_out, in_3);
  nand nand_6 (nand_6_out, nand_4_out, nand_5_out);
  nand nand_7 (nand_7_out, nand_5_out, in_3);
  or or_1 (Carry_Output, and_2_out, and_1_out);
  nand nand_8 (SUM, nand_6_out, nand_7_out);

  // Notes on the sheet:
  //   FULL ADDER
  //   XOR Gate using NAND Gate
  //   USING BASIC LOGIC AND UNIVERSAL GATES
  //   XOR Gate usig NAND Gate
  //   ASHUTOSH KUMAR
endmodule
